# Fritzing sketch Connections (saved by Fritzing 0.9.3b)
breadboards: 1

parts:
  FC-1 = Sound Sensor
  Part1 = Arduino Uno (Rev3)
  LED1 = LED - 3mm [color="Red (633nm)" package="3 mm [THT]"]
  R1 = Resistor [tolerance=±5% resistance=220 package=THT]

nets:
  VCC: FC-1.VCC, Part1.5V
  GND: FC-1.GND, Part1.GND
  N1: FC-1.OUT, Part1.A0
  N2: Part1.D7, LED1.anode, R1.Pin_0, R1.Pin_1
